# Fritzing sketch PN5180 Wiring (saved by Fritzing 1.0.3b)

parts:
  Part2 = PN5180-NFC
  M2 = ESP32S-HiLetgo [part_number=ESP32S-HiLetgo]
  Part3 = TXB0104 4-channel Bi-Directional Level Shifter
  Part4 = Arduino Uno (Rev3) - ICSP
  Part5 = PN5180-NFC

nets:
  5V: Part2.5V, M2.VIN
  N1: Part2.3.3V, M2.3.3
  N2: Part2.RST, M2.GPIO22
  N3: Part2.NSS, M2.GPIO21
  N4: Part2.MOSI, M2.GPIO23
  N5: Part2.MISO, M2.GPIO19
  N6: Part2.SCK, M2.GPIO18
  N7: Part2.BUSY, M2.GPIO5
  GND: Part2.GND, M2.GND
  5V_2: Part3.HV, Part4.5V, Part5.5V
  N8: Part3.B2, Part4.D13/SCK
  N9: Part3.B3, Part4.D11_PWM/MOSI
  N10: Part3.B4, Part4.D10_PWM/SS
  GND_2: Part3.GND, Part3.OE, Part4.GND
  N11: Part3.A4, Part5.NSS
  N12: Part3.A3, Part5.MOSI
  N13: Part3.A2, Part5.SCK
  3V3: Part3.LV, Part4.3V3, Part5.3.3V
  N14: Part4.ICSP_MISO, Part4.D12/MISO, Part5.MISO
  N15: Part4.D8, Part5.RST
  N16: Part4.D9_PWM, Part5.BUSY

notes:
  5V Device (e.g. Arduino UNO/Nano)
  3.3V Device (e.g ESP8266/ESP32)

custom parts:
  PN5180-NFC: RFID High Frequency IC card reader/writer based on the PN5180 chip from NXP.
  ESP32S-HiLetgo: HiLetgo ESP-WROOM-32 ESP32 ESP-32S Development Board 2.4GHz Dual-Mode WiFi + Bluetooth Dual Cores Microcontroller The ESP32 integrated with Antenna switches, RF Balun, power amplifiers, low-noise amplifiers, filters, and management modules, and the entire solution occupies the least area of PCB. 2.4 GHz Wi-Fi plus Bluetooth dual-mode chip, with TSMC Ultra-low power consumption 40nm technology,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
  TXB0104 4-channel Bi-Directional Level Shifter: Because the Arduino (and Basic Stamp) are 5V devices, and most modern sensors, displays, flash cards and modes are 3.3V-only, many makers find that they need to perform level shifting/conversion to protect the 3.3V device from 5V. Although one can use resistors to make a divider, for high speed transfers, the resistors can add a lot of slew and cause havoc that is tough to debug. For that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
